# Fritzing sketch CARS (saved by Fritzing 0.9.0b)
breadboards: 1

parts:
  Parte1 = Arduino Uno (Rev3)
  IC1 = L293D [package=THT]
  Parte2 = SRF05 Ultrasonic Rangefinder
  IR1 = TSOP312.., 314.. [package=THT]
  LED1 = LED - 5mm [color="White (4500K)" package="5 mm [THT]"]
  LED2 = LED - 5mm [color="White (4500K)" package="5 mm [THT]"]
  M1 = DC Motor
  M2 = DC Motor
  VCC1 = Battery block 9V

nets:
  N1: Parte1.D8, IC1.In_2
  N2: Parte1.D9_PWM, IC1.In_1
  N3: Parte1.D10_PWM/SS, IC1.Enable_1
  N4: Parte1.D11_PWM/MOSI, IC1.Enable_2
  N5: Parte1.D12/MISO, IC1.In_4
  N6: Parte1.D13/SCK, IC1.In_3
  GND: Parte1.GND, Parte2.GND, IR1.GND
  N7: Parte1.D2, IR1.Data
  N8: Parte1.D6_PWM, Parte2.Trig
  N9: Parte1.D7, Parte2.Echo
  N10: Parte1.3V3, IR1.Vs, LED1.anode, LED2.anode
  5V: Parte1.5V, Parte2.VCC
  N11: IC1.Out_1_(_Controlled_by_Enable_1_), M1.pin_1
  N12: IC1.0V, LED1.cathode, LED2.cathode, VCC1.-
  N13: IC1.Out_2_(_Controlled_by_Enable_1_), M1.pin_2
  N14: IC1.+Vmotor, IC1.+V, VCC1.+
  N15: IC1.Out_3_(_Controlled_by_Enable_2_), M2.pin_1
  N16: IC1.Out_4_(_Controlled_by_Enable_2_), M2.pin_2
