# Fritzing sketch diagrama_servo (saved by Fritzing 0.9.0b)
breadboards: 1

parts:
  Parte1 = Arduino Uno (Rev3)
  LED1 = smd LED [color="Red (633nm)" package="0603 [SMD]"]
  LED2 = smd LED [color="Yellow (595nm)" package="0603 [SMD]"]
  LED3 = smd LED [color="Blue (430nm)" package="0603 [SMD]"]  # not connected
  R1 = Resistor [tolerance=±5% resistance=220 package=THT]
  R3 = Resistor [tolerance=±5% resistance=220 package=THT]
  J1 = Basic Servo

nets:
  N1: Parte1.D9_PWM, J1.pulse
  N2: Parte1.D11_PWM/MOSI, R3.Pin_0
  N3: Parte1.D12/MISO, R1.Pin_0
  N4: Parte1.D13/SCK, LED1.anode
  GND: Parte1.GND, LED1.cathode, LED2.cathode, J1.gnd
  5V: Parte1.5V, J1.vcc
  N5: LED2.anode, R1.Pin_1
